# Fritzing sketch Balance Bot Circuit (saved by Fritzing 0.9.3b)
circuit board: 11.4164cm x 4.80424cm
breadboards: 1

parts:
  Part1 = InvenSense MPU6050
  R1 = Resistor [tolerance=±5% resistance=2.2 package=THT]
  R2 = Resistor [tolerance=±5% resistance=2.2 package=THT]
  D1 = Rectifier Diode [part_number=1N4001 package="300 mil [THT]"]
  R9 = Rotary Potentiometer (Large) [maximum_resistance=100kΩ package=THT]
  R10 = Rotary Potentiometer (Large) [maximum_resistance=100kΩ package=THT]
  R11 = Rotary Potentiometer (Large) [maximum_resistance=100kΩ package=THT]
  J3 = female pin header, 4 pins [form="♀ (female)"]
  J4 = female pin header, 3 pins [form="♀ (female)"]
  R6 = Resistor [tolerance=±5% resistance=2.2k package=THT]
  R7 = Resistor [tolerance=±5% resistance=2.2k package=THT]
  R8 = Resistor [tolerance=±5% resistance=2.2k package=THT]
  R12 = Resistor [tolerance=±5% resistance=1k package=THT]
  R13 = Resistor [tolerance=±5% resistance=1k package=THT]
  R14 = Resistor [tolerance=±5% resistance=1k package=THT]
  J5 = female pin header, 2 pins [form="♀ (female)"]
  Teensy1 = Teensy 3.6 (Basic)
  J6 = female pin header, 24 pins [form="♀ (female)"]  # not connected
  J7 = female pin header, 24 pins [form="♀ (female)"]  # not connected

nets:
  VCC: Part1.VCC, R9.leg2, R10.leg2, R11.leg2, Teensy1.3V3, Teensy1.3V3_1
  GND: Part1.GND, R9.leg1, R10.leg1, R11.leg1, J3.pin4, R6.Pin_1, R7.Pin_1, R8.Pin_1, J5.pin2, Teensy1.GND, Teensy1.GND1
  N1: Part1.SCL, Teensy1.A5/D19
  N2: Part1.SDA, Teensy1.A4/D18
  N3: Part1.INT, Teensy1.A3/D17
  N4: R1.Pin_0, J3.pin1
  N5: R1.Pin_1, Teensy1.D10
  N6: R2.Pin_0, J3.pin2
  N7: R2.Pin_1, Teensy1.D9
  N8: D1.cathode, J5.pin1, Teensy1.Vin
  N9: D1.anode, J3.pin3
  N10: R9.wiper, Teensy1.A2/D16
  N11: R10.wiper, Teensy1.A1/D15
  N12: R11.wiper, Teensy1.A0/D14
  N13: J4.pin1, R13.Pin_0
  N14: J4.pin2, R12.Pin_0
  N15: J4.pin3, R14.Pin_0
  N16: R6.Pin_0, R13.Pin_1, Teensy1.A9/D23
  N17: R7.Pin_0, R12.Pin_1, Teensy1.A8/D22
  N18: R8.Pin_0, R14.Pin_1, Teensy1.A7/D21

custom parts:
  Teensy 3.6 (Basic): The Teensy is a complete USB-based microcontoller development system, in a very small footprint, capable of implementing many types of projects. All programming is done via the USB port. No special programmer is needed, only a standard micro-USB cable and a PC or Macintosh with a USB port.
